# Fritzing sketch DrinkDispenserFinal (saved by Fritzing 1.0.6)
breadboards: 2

parts:
  Arduino = Arduino Uno (Rev3)
  Pump1 = DC Motor [voltage_(max)=6V voltage_(min)=3V]
  Pump2 = DC Motor [voltage_(max)=6V voltage_(min)=3V]
  Power_Supply = DC Power [voltage=12V internal_resistance=0.1Ω]  # not connected
  Q1 = PNP-Transistor [package="TO92 [THT]"]
  Q2 = PNP-Transistor [package="TO92 [THT]"]
  Potentiometer = Rotary Potentiometer (Small) [maximum_resistance=10kΩ knob_status=50% power=0.5W package=THT]
  OpticalEndstop = shaft encoder
  IR-MixerStick = fc-51 [package=THT]
  MixerStick = DC Motor [voltage_(max)=6V voltage_(min)=3V]
  Q3 = PNP-Transistor [package="TO92 [THT]"]
  SwitchButton = Pushbutton [package="[THT]"]
  ContinueButton = Pushbutton [package="[THT]"]
  PulldownSwitch = Resistor [tolerance=±5% power=0.25W resistance=10k package=THT]
  PulldownContinue = Resistor [tolerance=±5% power=0.25W resistance=10k package=THT]
  LED1 = LED - 5mm [color="Red (633nm)" current=0.030A package="5 mm [THT]"]
  LED2 = LED - 5mm [color="Red (633nm)" current=0.030A package="5 mm [THT]"]
  LED3 = LED - 5mm [color="Red (633nm)" current=0.030A package="5 mm [THT]"]
  LED4 = LED - 5mm [color="Red (633nm)" current=0.030A package="5 mm [THT]"]
  R1 = Resistor [tolerance=±5% power=0.25W resistance=1k package=THT]
  R2 = Resistor [tolerance=±5% power=0.25W resistance=1k package=THT]
  R3 = Resistor [tolerance=±5% power=0.25W resistance=1k package=THT]
  R4 = Resistor [tolerance=±5% power=0.25W resistance=1k package=THT]
  StepperMotorSpinningPlate = Stepper Motor - Bipolar
  StepperDriver = Pololu A4988 [package=SO16]
  ElectrolyticCapacitor = Electrolytic Capacitor [capacitance=1µF voltage=35V package="100 mil [THT, electrolytic]"]

nets (from the breadboard view):
  N1: Arduino.A2, OpticalEndstop.OUT
  N2: Arduino.A3, IR-MixerStick.pin1
  N3: Arduino.A5/SCL, Potentiometer.wiper
  N4: Arduino.D8, StepperDriver.STEP
  N5: Arduino.D9_PWM, ContinueButton.Pin_1, ContinueButton.Pin_2, PulldownContinue.Pin_0
  N6: Arduino.D10_PWM/SS, SwitchButton.Pin_1, SwitchButton.Pin_2, PulldownSwitch.Pin_0
  N7: Arduino.D11_PWM/MOSI, LED2.anode
  N8: Arduino.D12/MISO, LED3.anode
  N9: Arduino.D13/SCK, LED4.anode
  N10: Arduino.D4, Q1.B
  N11: Arduino.D5_PWM, Q2.B
  N12: Arduino.D6_PWM, Q3.B
  N13: Arduino.D7, StepperDriver.DIR
  5V: Arduino.5V, Pump1.pin_1, Pump2.pin_1, Q2.C, Potentiometer.leg2, OpticalEndstop.VCC, IR-MixerStick.pin3, MixerStick.pin_1, Q3.C, SwitchButton.Pin_3, SwitchButton.Pin_4, ContinueButton.Pin_3, ContinueButton.Pin_4, LED1.anode, StepperDriver.VDD
  GND: Arduino.GND, Q1.C, Potentiometer.leg1, OpticalEndstop.GND, IR-MixerStick.pin2, PulldownSwitch.Pin_1, PulldownContinue.Pin_1, R1.Pin_0, R2.Pin_0, R3.Pin_0, R4.Pin_0, StepperDriver.GND, ElectrolyticCapacitor.-
  N14: Arduino.VIN, StepperDriver.VMOT, ElectrolyticCapacitor.+
  N15: Pump1.pin_2, Q1.E
  N16: Pump2.pin_2, Q2.E
  N17: MixerStick.pin_2, Q3.E
  N18: LED1.cathode, R1.Pin_1
  N19: LED2.cathode, R2.Pin_1
  N20: LED3.cathode, R3.Pin_1
  N21: LED4.cathode, R4.Pin_1
  N22: StepperMotorSpinningPlate.A, StepperDriver.2B
  N23: StepperMotorSpinningPlate.C, StepperDriver.2A
  N24: StepperMotorSpinningPlate.B, StepperDriver.1A
  N25: StepperMotorSpinningPlate.D, StepperDriver.1B
